# Fritzing sketch Arduino_Mega_Schaltung (saved by Fritzing 0.9.3b)
breadboards: 1

parts:
  Bauteil1 = Arduino Mega 2560 (Rev3)
  RHT1 = Humidity and Temperature Sensor RHT03  # not connected
  R1 = Resistor [tolerance=±5% resistance=220 package="2010 [SMD]"]
  R2 = Resistor [tolerance=±5% resistance=220 package="2010 [SMD]"]
  Q1 = PNP-Transistor [package="TO92 [THT]"]
  J1 = Basic Servo
  S1 = Momentary Switch [package=ksa_sealed_tac_switch]
  R3 = Resistor [tolerance=±5% resistance=220 package="2010 [SMD]"]

nets:
  N1: Bauteil1.D9_PWM, S1.2, R3.Pin_0
  5V: Bauteil1.5V, R1.Pin_1, J1.vcc, S1.4
  N2: Bauteil1.GND, Q1.B, R3.Pin_1
  N3: Bauteil1.D2_PWM, J1.pulse
  N4: Bauteil1.D24, R1.Pin_0
  N5: Bauteil1.D25, R2.Pin_1
  N6: R2.Pin_0, Q1.E
  N7: Q1.C, J1.gnd

notes:
  ESP82666 WIFI Module
  OLED 128x64 Display 0.96" SSD1306 (I2C or SPI)
  used in I2C mode
  GND = Minus
  VCC = 5V
  D0 = SCL
  D1 = SDA
  RES = D8
  push button to switch the info screen
